# Fritzing sketch breadboard (saved by Fritzing 0.9.3b)
breadboards: 1

parts:
  Teensy_3_1 = Teensy 3.1
  S1 = Pushbutton [package="[THT]"]
  S2 = Pushbutton [package="[THT]"]
  S3 = Pushbutton [package="[THT]"]
  S4 = Pushbutton [package="[THT]"]
  S5 = Pushbutton [package="[THT]"]
  Grove1 = Grove OLED 128x96

nets:
  GND: Teensy_3_1.GND, Grove1.GND
  N1: Teensy_3_1.D8, S5.Pin_3, S5.Pin_4
  N2: Teensy_3_1.D9, S1.Pin_3, S1.Pin_4
  N3: Teensy_3_1.D10, S4.Pin_3, S4.Pin_4
  N4: Teensy_3_1.D11, S2.Pin_4
  N5: Teensy_3_1.D12, S3.Pin_3, S3.Pin_4
  N6: Teensy_3_1.A5/D19, Grove1.SDA
  N7: Teensy_3_1.A6/D20, Grove1.SCL
  3V3: Teensy_3_1.3V3, S1.Pin_1, S1.Pin_2, S2.Pin_1, S2.Pin_2, S3.Pin_1, S3.Pin_2, S4.Pin_1, S4.Pin_2, S5.Pin_1, S5.Pin_2, Grove1.VCC
